// Logisim project control-logic.circ as structural Verilog
module control_logic (
  input  [31:0] inst,
  input  BrEq,
  input  BrLt,
  output PCSel,
  output RegWEn,
  output [2:0] ImmSel,
  output BrUn,
  output ASel,
  output BSel,
  output [3:0] ALUSel,
  output MemRW,
  output [1:0] WBSel,
  output CSRSel,
  output CSRWen
);

  wire add, addi, and_1_out, and_6_out, and_7_out, and_9_out, and_10_out, and_11_out, and_12_out, and_14_out,
       and_17_out, and_19_out, and_20_out, and_22_out, and_23_out, and_24_out, and_25_out, and_26_out,
       and_27_out, and_28_out, and_29_out, and_40_out, and_41_out, and_42_out, and_44_out, and_45_out,
       and_55_out, and_61_out, auipc_inst, csrw_inst, csrwi_inst, Fc3_Is_0, Fc3_Is_1, Fc3_Is_2, Fc3_Is_3,
       Fc3_Is_4, Fc3_Is_5, Fc3_Is_6, Fc3_Is_7, Fc7_Is_0, Fc7_Is_0x20, Fc7_Is_1, is_add0, is_and7, is_bsel15,
       is_mul8, is_mulh9, is_mulhu11, is_OPC_0x6f, is_OPC_0x13, is_OPC_0x67, is_or6, is_sll1, is_slt2,
       is_sra13, is_srl5, is_sub12, is_xor4, IType, lui_inst, nor_2_out, nor_3_out, not_2_out, not_3_out,
       not_4_out, not_5_out, not_6_out, not_7_out, not_8_out, not_10_out, not_11_out, not_12_out, not_13_out,
       not_14_out, not_15_out, not_16_out, not_17_out, not_18_out, not_19_out, not_20_out, not_21_out,
       not_22_out, not_23_out, not_24_out, not_25_out, not_26_out, not_27_out, not_28_out, not_29_out,
       not_30_out, not_31_out, NotRegWEn, op_high_is_6, op_low_is_3, or_8_out, or_9_out, or_10_out,
       priority_encoder_1_gs, priority_encoder_2_gs, R_and_I, RType, Rtype_fc3_is0, Rtype_fc3_is1, SBType,
       sll_inst, slli_inst, slt_inst, slti_inst, UType, xor_inst, xori_inst;
  wire [15:0] rom_1_data;

  or or_1 (is_sll1, slli_inst, sll_inst);
  or or_2 (is_slt2, slti_inst, slt_inst);
  or or_3 (is_xor4, xor_inst, xori_inst);
  and and_1 (and_1_out, Fc3_Is_5, R_and_I);
  Priority_Encoder priority_encoder_1 (
    .in0(IType), .in1(MemRW), .in2(SBType), .in3(is_OPC_0x6f), .in4(UType), .out(ImmSel),
    .gs(priority_encoder_1_gs));  // open: in5, in6, in7, en_in, en_out
  ROM #(.addrWidth(6), .dataWidth(16)) rom_1 (.data(rom_1_data));  // open: addr
  nor nor_1 (BSel, RType, SBType);
  or or_4 (NotRegWEn, SBType, MemRW);
  and and_2 (is_sra13, inst[30], and_1_out);
  and and_3 (is_srl5, and_1_out, Fc7_Is_0);
  or or_5 (is_add0, add, WBSel[0], addi, MemRW, csrw_inst, SBType, auipc_inst, is_OPC_0x6f, is_OPC_0x67);
  or or_6 (R_and_I, RType, is_OPC_0x13);
  and and_4 (is_or6, Fc3_Is_6, R_and_I);
  and and_5 (is_and7, Fc3_Is_7, R_and_I);
  not not_1 (RegWEn, NotRegWEn);
  and and_6 (and_6_out, inst[5], inst[4]);
  nor nor_2 (nor_2_out, inst[3], inst[2]);
  not not_2 (not_2_out, inst[3]);
  not not_3 (not_3_out, inst[6]);
  not not_4 (not_4_out, inst[4]);
  and and_7 (and_7_out, inst[5], inst[6]);
  not not_5 (not_5_out, inst[4]);
  not not_6 (not_6_out, inst[4]);
  not not_7 (not_7_out, inst[6]);
  or or_7 (is_bsel15, lui_inst, csrwi_inst);
  and and_8 (op_high_is_6, not_4_out, and_7_out);
  or or_8 (or_8_out, inst[2], inst[3]);
  not not_8 (not_8_out, inst[6]);
  and and_9 (and_9_out, and_6_out, nor_2_out);
  and and_10 (and_10_out, inst[5], inst[6]);
  and and_11 (and_11_out, op_low_is_3, not_6_out);
  and and_12 (and_12_out, inst[5], not_7_out);
  Priority_Encoder #(.select(4)) priority_encoder_2 (
    .in0(is_add0), .in1(is_sll1), .in2(is_slt2), .in4(is_xor4), .in5(is_srl5), .in6(is_or6), .in7(is_and7),
    .in8(is_mul8), .in9(is_mulh9), .in11(is_mulhu11), .in12(is_sub12), .in13(is_sra13), .in15(is_bsel15),
    .out(ALUSel), .gs(priority_encoder_2_gs));  // open: in3, in10, in14, en_out, en_in
  not not_9 (op_low_is_3, or_8_out);
  and and_13 (RType, not_8_out, and_9_out);
  and and_14 (and_14_out, op_low_is_3, not_5_out);
  and and_15 (MemRW, and_11_out, and_12_out);
  and and_16 (lui_inst, inst[2], not_2_out, inst[4], inst[5], not_3_out);
  and and_17 (and_17_out, inst[2], not_10_out);
  not not_10 (not_10_out, inst[3]);
  nor nor_3 (nor_3_out, inst[5], inst[6]);
  and and_18 (SBType, and_14_out, and_10_out);
  and and_19 (and_19_out, and_17_out, inst[4]);
  and and_20 (and_20_out, inst[2], inst[3]);
  and and_21 (auipc_inst, and_19_out, nor_3_out);
  not not_11 (not_11_out, inst[12]);
  not not_12 (not_12_out, inst[13]);
  not not_13 (not_13_out, inst[14]);
  not not_14 (not_14_out, inst[13]);
  not not_15 (not_15_out, inst[14]);
  not not_16 (not_16_out, inst[12]);
  not not_17 (not_17_out, inst[14]);
  not not_18 (not_18_out, inst[14]);
  not not_19 (not_19_out, inst[12]);
  not not_20 (not_20_out, inst[13]);
  not not_21 (not_21_out, inst[13]);
  not not_22 (not_22_out, inst[12]);
  or or_9 (or_9_out, inst[25], inst[26]);
  and and_22 (and_22_out, not_11_out, not_12_out);
  and and_23 (and_23_out, inst[12], not_14_out);
  and and_24 (and_24_out, not_16_out, inst[13]);
  and and_25 (and_25_out, inst[12], inst[13]);
  and and_26 (and_26_out, not_19_out, not_20_out);
  and and_27 (and_27_out, inst[12], not_21_out);
  and and_28 (and_28_out, not_22_out, inst[13]);
  and and_29 (and_29_out, inst[12], inst[13]);
  not not_23 (not_23_out, or_9_out);
  not not_24 (not_24_out, inst[30]);
  and and_30 (is_OPC_0x6f, and_20_out, op_high_is_6);
  not not_25 (not_25_out, inst[4]);
  or or_10 (or_10_out, inst[5], inst[6]);
  not not_26 (not_26_out, inst[3]);
  and and_31 (Fc3_Is_0, and_22_out, not_13_out);
  and and_32 (Fc3_Is_1, and_23_out, not_15_out);
  and and_33 (Fc3_Is_2, and_24_out, not_17_out);
  and and_34 (Fc3_Is_3, and_25_out, not_18_out);
  and and_35 (Fc3_Is_4, and_26_out, inst[14]);
  and and_36 (Fc3_Is_5, and_27_out, inst[14]);
  and and_37 (Fc3_Is_6, and_28_out, inst[14]);
  and and_38 (Fc3_Is_7, and_29_out, inst[14]);
  and and_39 (Fc7_Is_0, not_23_out, not_24_out);
  not not_27 (not_27_out, or_10_out);
  and and_40 (and_40_out, inst[2], not_26_out);
  and and_41 (and_41_out, op_low_is_3, not_25_out);
  and and_42 (and_42_out, op_low_is_3, inst[4]);
  and and_43 (is_OPC_0x67, and_40_out, op_high_is_6);
  and and_44 (and_44_out, op_low_is_3, inst[4]);
  and and_45 (and_45_out, inst[5], inst[6]);
  and and_46 (WBSel[0], and_41_out, not_27_out);
  and and_47 (is_OPC_0x13, not_27_out, and_42_out);
  and and_48 (WBSel[1], and_44_out, and_45_out);
  or or_11 (UType, auipc_inst, lui_inst);
  and and_49 (Rtype_fc3_is0, RType, Fc3_Is_0);
  not not_28 (not_28_out, inst[26]);
  not not_29 (not_29_out, inst[30]);
  or or_12 (IType, WBSel[0], is_OPC_0x13, is_OPC_0x67, WBSel[1]);
  and and_50 (slli_inst, Fc3_Is_1, is_OPC_0x13);
  and and_51 (Rtype_fc3_is1, Fc3_Is_1, RType);
  and and_52 (slt_inst, RType, Fc3_Is_2);
  and and_53 (xor_inst, Fc3_Is_4, RType);
  and and_54 (xori_inst, Fc3_Is_4, is_OPC_0x13);
  and and_55 (and_55_out, inst[25], not_28_out);
  and and_56 (csrw_inst, WBSel[1], Fc3_Is_1);
  and and_57 (csrwi_inst, WBSel[1], Fc3_Is_5);
  and and_58 (add, Fc7_Is_0, Rtype_fc3_is0);
  and and_59 (addi, is_OPC_0x13, Fc3_Is_0);
  and and_60 (Fc7_Is_1, and_55_out, not_29_out);
  not not_30 (not_30_out, inst[25]);
  not not_31 (not_31_out, inst[26]);
  and and_61 (and_61_out, not_30_out, not_31_out);
  and and_62 (is_mul8, Fc7_Is_1, Rtype_fc3_is0);
  and and_63 (is_mulhu11, RType, Fc3_Is_3);
  and and_64 (sll_inst, Rtype_fc3_is1, Fc7_Is_0);
  and and_65 (is_mulh9, Rtype_fc3_is1, Fc7_Is_1);
  and and_66 (slti_inst, is_OPC_0x13, Fc3_Is_2);
  and and_67 (Fc7_Is_0x20, and_61_out, inst[30]);
  and and_68 (is_sub12, Fc7_Is_0x20, Rtype_fc3_is0);

  // Other names for the same wires on the sheet: is_OPC_0x03 = WBSel[0]; load = WBSel[0]; is_OPC_0x73 = WBSel[1];
  //   SType = MemRW; OP[6:0] = inst[6:0]; OPb0 = inst[0]; OPb1 = inst[1]; OPb2 = inst[2]; OPb3 = inst[3];
  //   OPb4 = inst[4]; OPb5 = inst[5]; OPb6 = inst[6]; rd[4:0] = inst[11:7]; Fc3_0 = inst[12];
  //   funct[2:0] = inst[14:12]; Fc3_1 = inst[13]; Fc3_2 = inst[14]; rs1[4:0] = inst[19:15];
  //   immShort[11:0] = inst[31:20]; rs2[4:0] = inst[24:20]; Fc7_0 = inst[25]; funct7[6:0] = inst[31:25];
  //   Fc7_1 = inst[26]; Fc7_5 = inst[30]; is_OPC_0x17 = auipc_inst; jal_inst = is_OPC_0x6f; JType = is_OPC_0x6f;
  //   mul_inst = is_mul8; mulh_inst = is_mulh9; mulhu_inst = is_mulhu11; sub_inst = is_sub12

  // Notes on the sheet:
  //   AUIPC
  //   jal
  //   jalr
  //   INPUTS to your circuit
  //   Connect ROM Input here ->
  //   BSEL
  //   RegWEn
  //   ROM FOR CONTROL LOGIC
  //   Imm-Sel
  //   MemRW
  //   WBSel
  //   DON'T CHANGE THE LOCATIONS OF THE INPUTS AND OUTPUTS!
  //   OUTPUT from your circuit
  //   CLOSE
  //   WIRE
  //   TO
  //   USE
  //   ROM
  //   AluSel
  //   Reminder: Use combinational logic for PCSel
  //   0x63
  //   0x37
  //   0x23
  //   AUIPC
  //   jal
  //   jalr
  //   csr
  //   I_Type
endmodule
